# Fritzing sketch 05_automatic-trash-can (saved by Fritzing 0.9.3b)
breadboards: 1

parts:
  Part1 = Arduino Uno (Rev3)
  hc-sr1 = hc-sr04
  J1 = Basic Servo

nets:
  N1: Part1.D9_PWM, hc-sr1.Trig
  N2: Part1.D10_PWM/SS, hc-sr1.Echo
  N3: Part1.D6_PWM, J1.pulse
  VCC: Part1.5V, hc-sr1.VCC, J1.vcc
  GND: Part1.GND, hc-sr1.GND, J1.gnd
