# Fritzing sketch automatic-lamp (saved by Fritzing 0.9.3b)

parts:
  Part1 = Arduino Uno (Rev3)
  e-radionica_com1 = LM393 LDR breakout [part_number=100027]
  Mod1 = KY-019 5V Relay Module [package="Breakout board"]
  LED1 = LEDs [package=led10mm]
  Power_plug1 = Power plug

nets:
  N1: Part1.A0, e-radionica_com1.AO
  N2: Part1.D12/MISO, Mod1.S
  GND: Part1.GND, e-radionica_com1.GND, Mod1.-
  5V: Part1.5V, e-radionica_com1.VCC, Mod1.+
  N3: Mod1.NC, LED1.A
  N4: Mod1.Common, Power_plug1.VCC
  N5: LED1.C, Power_plug1.GND

custom parts:
  KY-019 5V Relay Module: KY-019 5V Relay module, used to control AC circuits. (Special thanks to vanepp for fixing the PCB holes and other errors)
  LEDs: LEDs Standard schematic elements and footprints for 5mm, 3mm, 1206, and 0603 sized LEDs. 5mm - Spark Fun Electronics SKU : COM-00529 (and others)
