# Fritzing sketch light-follower (saved by Fritzing 0.9.3b)

parts:
  M1 = DC Motor
  M2 = DC Motor
  Part1 = Arduino Uno (Rev3)
  S1 = H-Bridge with L298N
  VCC1 = Battery block 9V
  e-radionica_com1 = LM393 LDR breakout [part_number=100027]
  e-radionica_com2 = LM393 LDR breakout [part_number=100027]

nets:
  N1: M1.pin_1, S1.M2-02
  N2: M1.pin_2, S1.M2-01
  N3: M2.pin_1, S1.M1-01
  N4: M2.pin_2, S1.M1-02
  N5: Part1.A0, e-radionica_com1.AO
  N6: Part1.A1, e-radionica_com2.AO
  GND: Part1.GND, S1.GND, VCC1.-, e-radionica_com1.GND, e-radionica_com2.GND
  N7: Part1.D2, S1.ENA
  N8: Part1.D3_PWM, S1.IN1
  5V: Part1.5V, S1.5V, e-radionica_com1.VCC, e-radionica_com2.VCC

custom parts:
  H-Bridge with L298N: h-bridge
