# Fritzing sketch servo-external-power (saved by Fritzing 0.9.3b)

parts:
  Part1 = Arduino Uno (Rev3)
  J1 = Basic Servo [part_number="12 V servo"]
  Power_plug1 = Power plug [part_number=12V]

nets:
  N1: Part1.D9_PWM, J1.pulse
  GND: Part1.GND, J1.gnd, Power_plug1.GND
  VCC: J1.vcc, Power_plug1.VCC
